# Fritzing sketch conexiones (saved by Fritzing 0.9.3b)
breadboards: 1

parts:
  Componente1 = KS0001 Uno (Rev3)
  U1 = ESP8266 WiFi Module [part_number=ESP8266]

nets:
  GND: Componente1.GND, U1.GND
  N1: Componente1.D0/RX, U1.RXD
  N2: Componente1.D1/TX, U1.TXD
  5V: Componente1.5V, U1.VCC, U1.CH_PD

notes:
  Los pines Tx y Rx deben ir cruzados
  Tx UNO -- Rx ESP01 -- Azul
  Rx UNO -- Tx ESP01 -- Verde

custom parts:
  ESP8266 WiFi Module: Generic WiFi Module based on the ESP8266 with onboard PCB antenna and UART communications
